// Digital circuit CPU.dig as structural Verilog
module CPU (
  input  Rise,
  input  Fall,
  input  [7:0] ROM,
  input  [7:0] MemIn,
  output [7:0] ROMAddr,
  output [7:0] MemAddr,
  output MemWrite,
  output [7:0] MemOut
);

  wire carry, control_1_p3, destMemAddr, destRa, setImmed, setRegs, zero;
  wire [1:0] alu_1_cout, control_1_p4, control_1_p8;
  wire [2:0] control_1_p6, control_1_p7;
  wire [3:0] Active_registers_q, control_1_p5;
  wire [7:0] GPRs_da, GPRs_db, Immediate_value_q, multiplexer_1_out, multiplexer_2_out, multiplexer_3_out,
       PC_Adder_s;

  // Control control_1: pin names not known; wires that end beside it: Rise, ROM[7:4], control_1_p3, control_1_p4, control_1_p5, control_1_p6, control_1_p7, control_1_p8
  Register #(.Bits(8)) Immediate_value (.D(ROM), .C(Rise), .en(setImmed), .Q(Immediate_value_q));
  Register #(.Bits(4)) Active_registers (.D(ROM[3:0]), .C(Rise), .en(setRegs), .Q(Active_registers_q));
  Decoder #(.Selector_Bits(2)) decoder_1 (
    .sel(control_1_p8), .out_0(MemWrite), .out_1(destMemAddr), .out_2(destRa));  // open: out_3
  // Probe Active rA on Active_registers_q[3:2]
  // Probe Active rB on Active_registers_q[1:0]
  RegisterFile #(.Bits(8)) GPRs (
    .Din(MemOut), .we(destRa), .Rw(Active_registers_q[3:2]), .C(Fall), .Ra(Active_registers_q[3:2]),
    .Rb(Active_registers_q[1:0]), .Da(GPRs_da), .Db(GPRs_db));
  Register #(.Bits(8), .isProgramCounter("true")) PC (.D(multiplexer_3_out), .C(Fall), .en(1'b1), .Q(ROMAddr));
  Multiplexer #(.Selector_Bits(3), .Bits(8)) multiplexer_1 (
    .sel(control_1_p6), .in_0(MemIn), .in_1(Immediate_value_q), .in_2(GPRs_da), .in_3(GPRs_db),
    .in_4(ROMAddr), .in_5(8'hbd), .in_6(8'hbd), .in_7(8'hbd), .out(multiplexer_1_out));
  Multiplexer #(.Selector_Bits(3), .Bits(8)) multiplexer_2 (
    .sel(control_1_p7), .in_0(MemIn), .in_1(Immediate_value_q), .in_2(GPRs_da), .in_3(GPRs_db),
    .in_4(ROMAddr), .in_5(8'hbd), .in_6(8'hbd), .in_7(8'hbd), .out(multiplexer_2_out));
  ALU alu_1 (
    .Mode(control_1_p5), .A(multiplexer_1_out), .B(multiplexer_2_out), .Cin(carry), .Cout(alu_1_cout[0]),
    .Zero(alu_1_cout[1]), .Out(MemOut));
  Register nextFetchMode (.D(control_1_p3), .C(Fall), .en(1'b1), .Q(setImmed));
  Add #(.Bits(8)) PC_Adder (.a(ROMAddr), .b(8'h1), .c_i(1'b0), .s(PC_Adder_s));  // open: c_o
  not not_1 (setRegs, setImmed);
  Register #(.Bits(2)) Status (.D(alu_1_cout), .C(Fall), .en(1'b1), .Q({zero, carry}));
  Register #(.Bits(8)) Memory_address (.D(MemOut), .C(Fall), .en(destMemAddr), .Q(MemAddr));
  Multiplexer #(.Selector_Bits(2), .Bits(8)) multiplexer_3 (
    .sel(control_1_p4), .in_0(ROMAddr), .in_1({8{1'b0}}), .in_2(PC_Adder_s), .in_3(MemOut),
    .out(multiplexer_3_out));

  // Other names for the same wires on the sheet: destMem = MemWrite; pc[7:0] = ROMAddr

  // Notes on the sheet:
  //   Rise > ready > fall
  //   Instruction decode
  //   Ready ASAP
  //   Data fetch
  //   Execute
  //   Fall > ready > next rise
  //   Fetch next instruction
  //   Write back
endmodule
