// Digital circuit Control.dig as structural Verilog
module Control (
  input  Rise,
  input  [3:0] Instruction,
  output NextFetchMode,
  output [1:0] PCMode,
  output [3:0] ALUMode,
  output [2:0] SrcA,
  output [2:0] SrcB,
  output [1:0] Dest
);

  wire \continue ;
  wire [7:0] Decision_d, multiplexer_1_out, uPC_q;

  Multiplexer #(.Bits(8)) multiplexer_1 (
    .sel(\continue ), .in_0({4'b0000, Instruction}), .in_1(Decision_d), .out(multiplexer_1_out));
  Register #(.Bits(8)) uPC (.D(multiplexer_1_out), .C(Rise), .en(1'b1), .Q(uPC_q));
  ROM #(.AddrBits(8), .Bits(8)) ControlLow (.A(uPC_q), .sel(1'b1), .D({ALUMode, PCMode, NextFetchMode, \continue }));
  ROM #(.AddrBits(8), .Bits(8)) ControlHigh (.A(uPC_q), .sel(1'b1), .D({Dest, SrcB, SrcA}));
  ROM #(.AddrBits(8), .Bits(8)) Decision (.A(uPC_q), .sel(1'b1), .D(Decision_d));
  // Probe uOP on uPC_q
  // Probe Continue uOP on \continue 

  // Notes on the sheet:
  //   NextFetchMode: Whether to prefetch active registersor immediate for the next cycle.
  //   A false/0 will fetch active registers at the beginning of the next cycle, 
  //   and a true/1 will fetch immediate at the beginning of the next cycle.
  //   This "prefetching" is done so that active registers are accessible at the first
  //   clock cycle of an instruction. This does mean that immediate values cannot 
  //   be used during the first cycle of an instruction, since the microcode may not
  //   have been decoded yet.
  //   contents of ControlLow (hex, n*v repeats v):
  //   b,1,1,251*0,8,8
  //   contents of ControlHigh (hex, n*v repeats v):
  //   0,43,43,250*0,2,80,81
  //   contents of Decision (hex, n*v repeats v):
  //   ff,fe,fd
endmodule
