// Digital circuit Main.dig as structural Verilog
module Main (
  input  Clock,
  input  Enable_clock
);

  wire and_1_out, cpu_1_p6, fall, Manual_pulse_out, or_1_out;
  wire [7:0] cpu_1_p3, cpu_1_p4, cpu_1_p5, cpu_1_p7, rom_1_d;

  Button Manual_pulse (.out(Manual_pulse_out));
  ROM #(.AddrBits(8), .Bits(8)) rom_1 (.A(cpu_1_p7), .sel(1'b1), .D(rom_1_d));
  and and_1 (and_1_out, Enable_clock, Clock);
  or or_1 (or_1_out, Manual_pulse_out, and_1_out);
  FallingEdgeDetector fallingedgedetector_1 (.In(or_1_out), .Out(fall));
  // CPU cpu_1: pin names not known; wires that end beside it: or_1_out, rom_1_d, cpu_1_p3, cpu_1_p4, cpu_1_p5, cpu_1_p6, cpu_1_p7
  RAMDualPort #(.AddrBits(8), .Bits(8)) ramdualport_1 (
    .A(cpu_1_p4), .Din(cpu_1_p5), .str(cpu_1_p6), .C(fall), .ld(1'b1), .D(cpu_1_p3));

  // Notes on the sheet:
  //   Clock: Hz: 10
endmodule
